// Digital circuit BeanBoardSPI-diagnostics.dig as structural Verilog
module BeanBoardSPI_diagnostics (
  input  D0,
  input  CLK,
  input  D1,
  input  D2,
  input  D3,
  input  D4,
  input  D5,
  input  D6,
  input  D7,
  input  RD,
  input  WR,
  input  IORQ,
  input  SER_IN,
  input  enable,
  input  A1,
  input  A2,
  input  A3,
  output D0_2,
  output D1_2,
  output D2_2,
  output D3_2,
  output D4_2,
  output D5_2,
  output D6_2,
  output D7_2,
  output SER_OUT,
  output SCK,
  output CS0,
  output CS1,
  output CS2,
  output CS3,
  output CS4,
  output CS5,
  output CS6,
  output CLK2
);

  wire _7474_1_pin2, _7474_1_pin5, _7474_1_pin8, _7474_1_pin9, _7474_2_pin2, _7474_2_pin5, _7474_2_pin8,
       _7474_2_pin9, _74138_1_pin10, _74138_1_pin11, _74161_1_pin11, _74161_1_pin12, _74161_1_pin13,
       _74161_1_pin14, and_1_out, count_clk, count_reset, ctrl_latch, int_clk, nand_1_out, nand_2_out,
       nand_3_out, nand_4_out, nand_5_out, nand_6_out, nand_7_out, nor_2_out, not_3_out, not_4_out, shift,
       srd, sreset, swr, swr_t, t1, t9;

  and and_1 (and_1_out, CLK2, enable);
  _7474 _7474_1 (
    .pin1(1'b1), .pin2(_7474_1_pin2), .pin3(CLK), .pin4(1'b1), .pin5(_7474_1_pin5), .pin6(_7474_1_pin2),
    .pin7(1'b0), .pin8(_7474_1_pin8), .pin9(_7474_1_pin9), .pin10(1'b1), .pin11(_7474_1_pin5),
    .pin12(_7474_1_pin8), .pin13(1'b1), .pin14(1'b1));
  // ScopeTrigger #(.maxStepCount(30)) scopetrigger_1: pin names not known; wires that end beside it: and_1_out
  Switch #(.Closed("true")) switch_1 (.A(_7474_1_pin9), .B(CLK2));
  Switch switch_2 (.A(_7474_1_pin5), .B(CLK2));
  Switch switch_3 (.A(CLK), .B(CLK2));
  Switch #(.Closed("true")) switch_4 (.A(SER_OUT), .B(SER_IN));
  assign D0_2 = ~WR ? D0 : 1'bz;  // DriverInvSel driverinvsel_1
  assign D1_2 = ~WR ? D1 : 1'bz;  // DriverInvSel driverinvsel_2
  assign D2_2 = ~WR ? D2 : 1'bz;  // DriverInvSel driverinvsel_3
  assign D3_2 = ~WR ? D3 : 1'bz;  // DriverInvSel driverinvsel_4
  assign D4_2 = ~WR ? D4 : 1'bz;  // DriverInvSel driverinvsel_5
  assign D5_2 = ~WR ? D5 : 1'bz;  // DriverInvSel driverinvsel_6
  assign D6_2 = ~WR ? D6 : 1'bz;  // DriverInvSel driverinvsel_7
  assign D7_2 = ~WR ? D7 : 1'bz;  // DriverInvSel driverinvsel_8
  _7474 _7474_2 (
    .pin1(1'b1), .pin2(_7474_2_pin2), .pin3(CLK2), .pin4(1'b1), .pin5(_7474_2_pin5), .pin6(_7474_2_pin2),
    .pin7(1'b0), .pin8(_7474_2_pin8), .pin9(_7474_2_pin9), .pin10(1'b1), .pin11(_7474_2_pin5),
    .pin12(_7474_2_pin8), .pin13(1'b1), .pin14(1'b1));
  Switch #(.Closed("true")) switch_5 (.A(_7474_2_pin9), .B(int_clk));
  Switch switch_6 (.A(_7474_2_pin5), .B(int_clk));
  Switch switch_7 (.A(CLK2), .B(int_clk));
  // Probe int-clk on int_clk
  _74299 _74299_1 (
    .pin1(shift), .pin2(srd), .pin3(srd), .pin4(D6_2), .pin5(D4_2), .pin6(D2_2), .pin7(D0_2), .pin9(sreset),
    .pin10(1'b0), .pin11(SER_IN), .pin12(int_clk), .pin13(D1_2), .pin14(D3_2), .pin15(D5_2), .pin16(D7_2),
    .pin17(SER_OUT), .pin18(1'b0), .pin19(swr_t), .pin20(1'b1));  // open: pin8
  _74138 _74138_1 (
    .pin1(A1), .pin2(A2), .pin3(A3), .pin4(IORQ), .pin5(IORQ), .pin6(1'b1), .pin8(1'b0),
    .pin10(_74138_1_pin10), .pin11(_74138_1_pin11), .pin16(1'b1));  // open: pin7, pin9, pin12, pin13, pin14, pin15
  nor nor_1 (ctrl_latch, WR, _74138_1_pin11);
  nor nor_2 (nor_2_out, RD, _74138_1_pin10);
  nor nor_3 (swr_t, _74138_1_pin10, WR);
  _74161 _74161_1 (
    .pin1(count_reset), .pin2(count_clk), .pin3(1'b0), .pin4(1'b0), .pin5(1'b0), .pin6(1'b0), .pin7(1'b1),
    .pin8(1'b0), .pin9(1'b1), .pin10(1'b1), .pin11(_74161_1_pin11), .pin12(_74161_1_pin12),
    .pin13(_74161_1_pin13), .pin14(_74161_1_pin14), .pin16(1'b1));  // open: pin15
  not not_1 (srd, nor_2_out);
  not not_2 (swr, swr_t);
  _7442 _7442_1 (
    .pin2(t1), .pin8(1'b0), .pin11(t9), .pin12(_74161_1_pin11), .pin13(_74161_1_pin12),
    .pin14(_74161_1_pin13), .pin15(_74161_1_pin14), .pin16(1'b1));  // open: pin1, pin3, pin4, pin5, pin6, pin7, pin9, pin10
  nand nand_1 (nand_1_out, t9, sreset);
  not not_3 (not_3_out, nand_1_out);
  nand nand_2 (nand_2_out, swr, nand_3_out);
  nand nand_3 (nand_3_out, nand_2_out, not_3_out);
  nand nand_4 (nand_4_out, t1, nand_5_out);
  nand nand_5 (nand_5_out, nand_4_out, not_3_out);
  _74373 _74373_1 (
    .pin1(1'b0), .pin2(sreset), .pin3(D0_2), .pin4(D1_2), .pin5(CS0), .pin6(CS1), .pin7(D2_2), .pin8(D3_2),
    .pin9(CS2), .pin10(1'b0), .pin11(ctrl_latch), .pin12(CS3), .pin13(D4_2), .pin14(D5_2), .pin15(CS4),
    .pin16(CS5), .pin17(D6_2), .pin18(D7_2), .pin19(CS6), .pin20(1'b1));
  nand nand_6 (nand_6_out, swr, sreset);
  not not_4 (not_4_out, nand_3_out);
  nand nand_7 (nand_7_out, not_4_out, int_clk);
  nor nor_4 (SCK, int_clk, nand_5_out);
  nand nand_8 (shift, nand_5_out, swr);
  not not_5 (count_reset, nand_6_out);
  not not_6 (count_clk, nand_7_out);

  // Other names for the same wires on the sheet: cs_0 = CS0; cs_1 = CS1; cs_2 = CS2; cs_3 = CS3; cs_4 = CS4;
  //   cs_5 = CS5; cs_6 = CS6; d0_t = D0_2; d1_t = D1_2; d2_t = D2_2; d3_t = D3_2; d4_t = D4_2; d5_t = D5_2;
  //   d6_t = D6_2; d7_t = D7_2; sclk = SCK

  // Notes on the sheet:
  //   D0: default 1
  //   D1: default 1
  //   D2: default 1
  //   D3: default 1
  //   D4: default 1
  //   D5: default 1
  //   D6: default 1
  //   D7: default 1
  //   RD: default 1
  //   WR: default 1
  //   IORQ: default 1
  //   A3: default 1
  //   Z80
  //   SPI
  //   Ctrl
  //   Bits
  //   reset
  //   cs0
  //   cs1
  //   cs2
  //   cs3
  //   cs4
  //   cs5
  //   cs6
  //   Clock Divider
  //   I/O Shift Register
  //   Port Decoding
  //   Counter / Decoder
  //   Control Logic
  //   SPI Control Register
endmodule
