// Digital circuit flipflop.dig as structural Verilog
module flipflop (
  input  CLK,
  input  set,
  input  reset,
  output clk_4,
  output clk_2,
  output clk_3
);

  wire _7474_1_pin2, _7474_1_pin8;

  // ScopeTrigger #(.maxStepCount(30)) scopetrigger_1: pin names not known; wires that end beside it: CLK
  _7474 _7474_1 (
    .pin1(reset), .pin2(_7474_1_pin2), .pin3(CLK), .pin4(set), .pin5(clk_2), .pin6(_7474_1_pin2),
    .pin7(1'b0), .pin8(_7474_1_pin8), .pin9(clk_4), .pin10(set), .pin11(clk_2), .pin12(_7474_1_pin8),
    .pin13(reset), .pin14(1'b1));

  assign clk_3 = CLK;

  // Notes on the sheet:
  //   set: default 1
  //   reset: default 1
endmodule
